// Logisim project 8bitcomputer.circ as structural Verilog: 1 circuit, main circuit main
// CLK
module main (
);

  wire bitselector_1_out, CLK_out, d_ff_1_q, d_ff_1_qn, demultiplexer_1_out0, demultiplexer_1_out1;
  wire [1:0] bitselector_2_out, bitselector_3_out, bitselector_4_out, bitselector_5_out;
  wire [7:0] adder_1_out, counter_1_q, divider_1_out, IR_q, multiplexer_1_out, multiplexer_2_out,
       multiplexer_3_out, multiplexer_4_out, multiplier_1_out, R0_q, R1_q, R2_q, register_1_q, register_2_q,
       rom_1_data, subtractor_1_out;

  Clock CLK (.out(CLK_out));
  Counter counter_1 (.up(d_ff_1_q), .count(d_ff_1_q), .clk(CLK_out), .Q(counter_1_q));  // open: clr, load, D, carry
  Register register_1 (.D({8{1'b0}}), .en(1'b1), .clk(CLK_out), .Q(register_1_q));  // open: clr
  Register R0 (.D(8'h1), .en(1'b1), .clk(CLK_out), .Q(R0_q));  // open: clr
  Demultiplexer #(.enable("false")) demultiplexer_1 (
    .out0(demultiplexer_1_out0), .out1(demultiplexer_1_out1), .in(d_ff_1_q), .sel(bitselector_1_out));
  Register #(.trigger("falling")) R1 (
    .D(register_2_q), .en(demultiplexer_1_out0), .clk(CLK_out), .Q(R1_q));  // open: clr
  ROM rom_1 (.addr(counter_1_q), .data(rom_1_data));
  Register #(.trigger("falling")) R2 (
    .D(register_2_q), .en(demultiplexer_1_out1), .clk(CLK_out), .Q(R2_q));  // open: clr
  BitSelector #(.width(2)) bitselector_1 (.in(bitselector_2_out), .out(bitselector_1_out), .sel(1'b0));
  Multiplexer #(.enable("false"), .select(2), .width(8)) multiplexer_1 (
    .in0(register_1_q), .in1(R0_q), .in2(R1_q), .in3(R2_q), .out(multiplexer_1_out), .sel(bitselector_3_out));
  Multiplexer #(.enable("false"), .select(2), .width(8)) multiplexer_2 (
    .in0(register_1_q), .in1(R0_q), .in2(R1_q), .in3(R2_q), .out(multiplexer_2_out), .sel(bitselector_4_out));
  Register IR (.D(rom_1_data), .en(d_ff_1_qn), .clk(CLK_out), .Q(IR_q));  // open: clr
  BitSelector #(.group(2)) bitselector_2 (.in(multiplexer_3_out), .out(bitselector_2_out), .sel(2'b10));
  Multiplexer #(.enable("false"), .width(8)) multiplexer_3 (
    .in0(IR_q), .in1({8{1'b0}}), .out(multiplexer_3_out), .sel(d_ff_1_qn));
  Adder adder_1 (.a(multiplexer_1_out), .b(multiplexer_2_out), .out(adder_1_out));  // open: cin, cout
  Subtractor subtractor_1 (.a(multiplexer_1_out), .b(multiplexer_2_out), .out(subtractor_1_out));  // open: bin, bout
  Multiplier multiplier_1 (.a(multiplexer_1_out), .b(multiplexer_2_out), .out(multiplier_1_out));  // open: cin, cout
  Divider divider_1 (.a(multiplexer_1_out), .b(multiplexer_2_out), .out(divider_1_out));  // open: upper, rem
  BitSelector #(.group(2)) bitselector_3 (.in(multiplexer_3_out), .out(bitselector_3_out), .sel(2'b01));
  BitSelector #(.group(2)) bitselector_4 (.in(multiplexer_3_out), .out(bitselector_4_out), .sel(2'b00));
  BitSelector #(.group(2)) bitselector_5 (.in(multiplexer_3_out), .out(bitselector_5_out), .sel(2'b11));
  Multiplexer #(.enable("false"), .select(2), .width(8)) multiplexer_4 (
    .in0(adder_1_out), .in1(subtractor_1_out), .in2(multiplier_1_out), .in3(divider_1_out),
    .out(multiplexer_4_out), .sel(bitselector_5_out));
  D_Flip_Flop d_ff_1 (.D(d_ff_1_qn), .clk(CLK_out), .Q(d_ff_1_q), .Qn(d_ff_1_qn));  // open: preset, reset
  Register #(.trigger("high")) register_2 (.D(multiplexer_4_out), .clk(CLK_out), .Q(register_2_q));  // open: en, clr

  // Notes on the sheet:
  //   PC-UP
  //   PC-EN
  //   0 const
  //   REG-DEST
  //   contents of rom_1 (hex, n*v repeats v):
  //   25 ba bb ae 3b 3d 25 bb be b0
  //   SRC-A
  //   SRC-B
  //   IR-WE
  //   ALU-OPCODE
endmodule
